# Fritzing sketch Design (saved by Fritzing 0.9.4)
breadboards: 1

parts:
  M1 = Arduino Uno WIFI REV2
  M2 = DC Motor
  M5 = DC Motor
  L298N1 = L298N DC motor driver
  L298N2 = L298N DC motor driver
  M6 = DC Motor
  M7 = DC Motor
  VCC1 = Battery
  Stromversorgung_Beradboard1 = Stromversorgung Beradboard [package=THT]
  Espessif_Serial_Wifi_Modul_1 = ESP8266 ESP01 [part_number=ESP8266 package=THT]  # not connected

nets:
  N1: M1.5V, Stromversorgung_Beradboard1.Ground_1#14
  N2: M1.GND, Stromversorgung_Beradboard1.+5_/_+3_Volt_4#12
  N3: M2.pin_1, L298N1.OUT2
  N4: M2.pin_2, L298N1.OUT1
  N5: M5.pin_1, L298N1.OUT4
  N6: M5.pin_2, L298N1.OUT3
  N7: L298N2.OUT1, M6.pin_2
  N8: L298N2.OUT2, M6.pin_1
  N9: L298N2.OUT3, M7.pin_2
  N10: L298N2.OUT4, M7.pin_1
  N11: VCC1.-, Stromversorgung_Beradboard1.+5_/_+3_Volt_4#13
  N12: VCC1.+, Stromversorgung_Beradboard1.Ground_1#15

custom parts:
  Arduino Uno WIFI REV2: The Arduino Uno WIFI REV2 is a microcontroller board based on the ATmega 4809. It has 14 digital input/output pins (of which 5 can be used as PWM outputs), 6 analog inputs, a 16 MHz ceramic resonator, a USB connection, a power jack, an ICSP header, and a reset button. It also has a WIFI controller with a secure ECC608 crypto unit and an internal IMU. It contains everything needed to support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
  L298N DC motor driver: 2x DC motor driver with 78M05 positive voltage regulator (7..35 V) L298N: max 46 V, 2 A Set 5 V Enable jumper to enable 5 V regultor (needed for the L298N) and +5 V output at screw terminal or supply external +5 V at screw terminal Set ENA and/or ENB to +5 V to enable motor permanently or supply ENA and/or ENB with PWM signal IN1 and IN2 set rotation directory for motor A (OUT1/OUT2) IN2 and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
  ESP8266 ESP01: Generic WiFi Module based on the ESP8266 with onboard PCB antenna and UART communications
